// Logisim project MiniALU.circ as structural Verilog: 5 circuits, main circuit main
module main (
  input  in_1,
  input  [7:0] in_2,
  input  in_3
);

  wire clock_1_out, opcodedecoder_1_rwrite;
  wire [7:0] alu_1_add, programcounter_1_pc, registers_1_bout, registers_1_cout, rom_1_data, rom_1_data_2,
       rom_1_data_3;
  wire [31:24] rom_1_data_4;

  Clock clock_1 (.out(clock_1_out));
  ROM #(.dataWidth(32)) rom_1 (
    .addr(programcounter_1_pc), .data({rom_1_data_4, rom_1_data_3, rom_1_data_2, rom_1_data}));
  ProgramCounter programcounter_1 (
    .Clear(in_1), .Clock(clock_1_out), .LoadValue(in_2), .EnableLoad(in_3), .PC(programcounter_1_pc));
  Registers registers_1 (
    .Clock(clock_1_out), .WriteEnable(opcodedecoder_1_rwrite), .Clear(in_1), .Value(alu_1_add),
    .Aaddress(rom_1_data), .Baddress(rom_1_data_2), .Caddress(rom_1_data_3), .Bout(registers_1_bout),
    .Cout(registers_1_cout));  // open: Aout
  ALU alu_1 (
    .A(registers_1_cout), .B(registers_1_bout), .Opcode(rom_1_data_4), .ADD(alu_1_add[0]));  // open: Result, SUB, MUL, DIV, MODx, NOTx, ANDx, ORx, XORx, EQ, NEQ, GTE, LTE, GT, LT
  OpcodeDecoder opcodedecoder_1 (.Opcode(rom_1_data_4), .RWrite(opcodedecoder_1_rwrite));  // open: Jump
  // Pins of 1 and 8 bits meet at alu_1_add

  // Notes on the sheet:
  //   contents of rom_1 (hex, n*v repeats v):
  //   400101ff 400000ff 10000001 10000001 10000001 400100ff
endmodule

module OpcodeDecoder (
  input  [7:0] Opcode,
  output RWrite,
  output Jump
);

  wire and_2_out, xor_1_out;

  xor xor_1 (xor_1_out, Opcode[4], Opcode[5]);
  and and_1 (RWrite, xor_1_out, and_2_out);
  and and_2 (and_2_out, ~Opcode[6], ~Opcode[7]);  // AND_Gate
endmodule

module ProgramCounter (
  input  Clear,
  input  Clock,
  input  [7:0] LoadValue,
  input  EnableLoad,
  output [7:0] PC
);

  wire n74161_1_pin1, n74161_1_pin15, n74161_2_pin1, not_1_out;

  not not_1 (not_1_out, EnableLoad);
  _74161 u_74161_1 (
    .pin1(n74161_1_pin1), .pin2(Clock), .pin3(LoadValue[0]), .pin4(LoadValue[1]), .pin5(LoadValue[2]),
    .pin6(LoadValue[3]), .pin7(not_1_out), .pin15(n74161_1_pin15), .pin14(PC[0]), .pin13(PC[1]),
    .pin12(PC[2]), .pin11(PC[3]), .pin10(not_1_out), .pin9(not_1_out));
  not not_2 (n74161_1_pin1, Clear);
  _74161 u_74161_2 (
    .pin1(n74161_2_pin1), .pin2(n74161_1_pin15), .pin3(LoadValue[4]), .pin4(LoadValue[5]),
    .pin5(LoadValue[6]), .pin6(LoadValue[7]), .pin7(not_1_out), .pin14(PC[4]), .pin13(PC[5]), .pin12(PC[6]),
    .pin11(PC[7]), .pin10(not_1_out), .pin9(not_1_out));  // open: pin15
  not not_3 (n74161_2_pin1, Clear);
endmodule

module ALU (
  input  [7:0] A,
  input  [7:0] B,
  input  [7:0] Opcode,
  output ADD,
  output [7:0] Result,
  output SUB,
  output MUL,
  output DIV,
  output MODx,
  output NOTx,
  output ANDx,
  output ORx,
  output XORx,
  output EQ,
  output NEQ,
  output GTE,
  output LTE,
  output GT,
  output LT
);

  wire not_1_out, not_2_out, not_3_out, not_4_out;
  wire [7:0] bit_extender_1_out, xor_1_out;

  not not_1 (not_1_out, Opcode[3]);
  not not_2 (not_2_out, Opcode[2]);
  not not_3 (not_3_out, Opcode[1]);
  not not_4 (not_4_out, Opcode[0]);
  and and_1 (ADD, not_4_out, not_3_out, not_2_out, Opcode[4]);
  and and_2 (SUB, Opcode[0], not_3_out, Opcode[4]);
  and and_3 (MUL, Opcode[1], not_4_out, Opcode[4]);
  and and_4 (DIV, Opcode[1], Opcode[0], Opcode[4]);
  and and_5 (MODx, Opcode[2], Opcode[4]);
  and and_6 (NOTx, not_4_out, not_3_out, not_2_out, not_1_out, Opcode[5]);
  and and_7 (ANDx, Opcode[0], not_3_out, not_2_out, not_1_out, Opcode[5]);
  and and_8 (ORx, Opcode[1], not_4_out, not_2_out, Opcode[5]);
  and and_9 (XORx, Opcode[1], Opcode[0], not_2_out, Opcode[5]);
  and and_10 (EQ, Opcode[2], not_4_out, not_3_out, Opcode[5]);
  and and_11 (NEQ, Opcode[2], Opcode[0], not_3_out);
  and and_12 (GTE, Opcode[2], Opcode[1], not_4_out);
  and and_13 (LTE, Opcode[2], Opcode[1], Opcode[0]);
  and and_14 (GT, Opcode[3], not_4_out);
  and and_15 (LT, Opcode[3], Opcode[0]);
  assign xor_1_out = B ^ bit_extender_1_out;  // XOR_Gate xor_1, 8 bits wide
  assign bit_extender_1_out = {{7{SUB}}, SUB};  // Bit_Extender bit_extender_1
  Adder adder_1 (.a(A), .b(xor_1_out), .out(Result));  // open: cin, cout
  Multiplier multiplier_1 ();  // open: a, b, out, cin, cout
endmodule

module Registers (
  input  Clock,
  input  WriteEnable,
  input  Clear,
  input  [7:0] Value,
  input  [7:0] Aaddress,
  input  [7:0] Baddress,
  input  [7:0] Caddress,
  output [7:0] Aout,
  output [7:0] Bout,
  output [7:0] Cout
);

  wire and_1_out, decoder_1_out0, decoder_1_out1, decoder_1_out2, decoder_1_out3, decoder_1_out4,
       decoder_1_out5, decoder_1_out6, decoder_1_out7;
  wire [7:0] R0_q, R1_q, R2_q, R3_q, R4_q, R5_q, R6_q, RSP_q;

  Decoder #(.enable("false"), .select(3)) decoder_1 (
    .out0(decoder_1_out0), .out1(decoder_1_out1), .out2(decoder_1_out2), .out3(decoder_1_out3),
    .out4(decoder_1_out4), .out5(decoder_1_out5), .out6(decoder_1_out6), .out7(decoder_1_out7),
    .sel(Caddress[2:0]));
  and and_1 (and_1_out, Clock, WriteEnable);
  Register RSP (.D(Value), .en(decoder_1_out7), .Q(RSP_q), .clk(and_1_out), .clr(Clear));
  Register R6 (.D(Value), .en(decoder_1_out6), .Q(R6_q), .clk(and_1_out), .clr(Clear));
  Register R5 (.D(Value), .en(decoder_1_out5), .Q(R5_q), .clk(and_1_out), .clr(Clear));
  Register R4 (.D(Value), .en(decoder_1_out4), .Q(R4_q), .clk(and_1_out), .clr(Clear));
  Register R3 (.D(Value), .en(decoder_1_out3), .Q(R3_q), .clk(and_1_out), .clr(Clear));
  Register R2 (.D(Value), .en(decoder_1_out2), .Q(R2_q), .clk(and_1_out), .clr(Clear));
  Register R1 (.D(Value), .en(decoder_1_out1), .Q(R1_q), .clk(and_1_out), .clr(Clear));
  Register R0 (.D(Value), .en(decoder_1_out0), .Q(R0_q), .clk(and_1_out), .clr(Clear));
  Multiplexer #(.select(3), .width(8)) multiplexer_1 (
    .in0(R0_q), .in1(R1_q), .in2(R2_q), .in3(R3_q), .in4(R4_q), .in5(R5_q), .in6(R6_q), .in7(RSP_q),
    .out(Aout), .sel(Aaddress[2:0]));
  Multiplexer #(.select(3), .width(8)) multiplexer_2 (
    .in0(R0_q), .in1(R1_q), .in2(R2_q), .in3(R3_q), .in4(R4_q), .in5(R5_q), .in6(R6_q), .in7(RSP_q),
    .out(Bout), .sel(Baddress[2:0]));
  Multiplexer #(.select(3), .width(8)) multiplexer_3 (
    .in0(R0_q), .in1(R1_q), .in2(R2_q), .in3(R3_q), .in4(R4_q), .in5(R5_q), .in6(R6_q), .in7(RSP_q),
    .out(Cout), .sel(Caddress[2:0]));
endmodule
